// Digital circuit ALU.dig as structural Verilog
module ALU (
  input  [3:0] A,
  input  [3:0] B,
  input  [1:0] S0_S1,
  input  [3:0] C,
  output [3:0] out_5,
  output [3:0] out_6
);

  wire [3:0] multiplexer_1_out, not_1_out, not_2_out;

  assign not_1_out = ~4'b0000;  // Not not_1, 4 bits wide
  Multiplexer #(.Selector_Bits(2), .Bits(4)) multiplexer_1 (
    .sel(S0_S1), .in_0(B), .in_1(not_2_out), .in_2(4'b0000), .in_3(not_1_out), .out(multiplexer_1_out));
  assign not_2_out = ~B;  // Not not_2, 4 bits wide
  // test test_1: pin names not known; wires that end beside it: A, multiplexer_1_out, C, out_5, out_6
endmodule
