// Digital circuit Register_bank.dig as structural Verilog
module Register_bank (
  input  clk,
  input  [1:0] ReadRegister_1,
  input  [1:0] ReadRegister_2,
  input  [7:0] Control_Signals,
  input  [3:0] WriteData,
  input  [1:0] WriteRegister,
  output [3:0] ReadData_1,
  output [3:0] ReadData_2
);

  wire [3:0] demultiplexer_1_out_0, demultiplexer_1_out_1, demultiplexer_1_out_2, demultiplexer_1_out_3,
       R0_p4, R1_p4, R2_p4, R3_p4;

  Demultiplexer #(.Bits(4), .Selector_Bits(2)) demultiplexer_1 (
    .sel(WriteRegister), .in(WriteData), .out_0(demultiplexer_1_out_0), .out_1(demultiplexer_1_out_1),
    .out_2(demultiplexer_1_out_2), .out_3(demultiplexer_1_out_3));
  // GRegister R0: pin names not known; wires that end beside it: demultiplexer_1_out_0, clk, Control_Signals[1:0], R0_p4
  // GRegister R1: pin names not known; wires that end beside it: demultiplexer_1_out_1, clk, Control_Signals[3:2], R1_p4
  // GRegister R2: pin names not known; wires that end beside it: demultiplexer_1_out_2, clk, Control_Signals[5:4], R2_p4
  // GRegister R3: pin names not known; wires that end beside it: demultiplexer_1_out_3, clk, Control_Signals[7:6], R3_p4
  Multiplexer #(.Bits(4), .Selector_Bits(2)) multiplexer_1 (
    .sel(ReadRegister_1), .in_0(R0_p4), .in_1(R1_p4), .in_2(R2_p4), .in_3(R3_p4), .out(ReadData_1));
  Multiplexer #(.Selector_Bits(2), .Bits(4)) multiplexer_2 (
    .sel(ReadRegister_2), .in_0(R0_p4), .in_1(R1_p4), .in_2(R2_p4), .in_3(R3_p4), .out(ReadData_2));
endmodule
